// Logisim project Traffic Lights for a two way roads.circ as structural Verilog: 1 circuit, main circuit main
module main (
  input  in_1
);

  wire and_1_out, and_2_out, and_3_out, and_4_out, and_5_out, and_6_out, and_7_out, clock_1_out, d_ff_1_q,
       d_ff_1_qn, d_ff_2_q, d_ff_2_qn, d_ff_3_q, d_ff_3_qn, not_1_out, or_1_out, or_2_out, or_3_out;

  not not_1 (not_1_out, in_1);
  Clock clock_1 (.out(clock_1_out));
  and and_1 (and_1_out, d_ff_1_q, d_ff_3_q);
  and and_2 (and_2_out, not_1_out, d_ff_2_qn);
  and and_3 (and_3_out, d_ff_1_qn, not_1_out);
  or or_1 (or_1_out, and_3_out, d_ff_3_q);
  or or_2 (or_2_out, and_1_out, d_ff_2_qn);
  or or_3 (or_3_out, and_2_out, d_ff_3_qn);
  D_Flip_Flop d_ff_1 (.clk(clock_1_out), .D(or_3_out), .Q(d_ff_1_q), .Qn(d_ff_1_qn), .en(1'b1));  // open: preset, reset
  D_Flip_Flop d_ff_2 (.clk(clock_1_out), .D(or_1_out), .Q(d_ff_2_q), .Qn(d_ff_2_qn), .en(1'b1));  // open: preset, reset
  D_Flip_Flop d_ff_3 (.clk(clock_1_out), .D(or_2_out), .Q(d_ff_3_q), .Qn(d_ff_3_qn), .en(1'b1));  // open: preset, reset
  and and_4 (and_4_out, d_ff_1_qn, d_ff_3_qn);
  and and_5 (and_5_out, d_ff_2_qn, d_ff_3_q);
  and and_6 (and_6_out, d_ff_1_qn, d_ff_3_q);
  and and_7 (and_7_out, d_ff_2_qn, d_ff_3_qn);
  LED led_1 (.in(d_ff_1_q));
  LED led_2 (.in(and_4_out));
  LED led_3 (.in(and_6_out));
  LED led_4 (.in(d_ff_2_q));
  LED led_5 (.in(and_5_out));
  LED led_6 (.in(and_7_out));

  // Notes on the sheet:
  //   BUSY CASE:
  //   QUIET CASE:
  //   -
  //   R1G2->R1A2->G1R2->A1R2
  //   R1G2->R1A2->R1R2->G1R2->A1R2->R1R2
  //   R1
  //   A1
  //   G1
  //   R2
  //   A2
  //   G2
endmodule
